# Fritzing sketch Trombino (saved by Fritzing 0.8.5b)
stripboards: 2
breadboards: 1

parts:
  R1 = Resistor [tolerance=±5% resistance=10k package=THT]
  R2 = Resistor [tolerance=±5% resistance=10k package=THT]
  R3 = Resistor [tolerance=±5% resistance=10k package=THT]
  S1 = Pushbutton [package="[THT]"]
  S2 = Pushbutton [package="[THT]"]
  S3 = Pushbutton [package="[THT]"]
  Part1 = Arduino Uno (Rev3)
  LED1 = LED - 5mm [color="Red (633nm)" package="5 mm [THT]"]
  LED2 = LED - 5mm [color="Yellow (595nm)" package="5 mm [THT]"]
  LED3 = LED - 5mm [color="Green (570nm)" package="5 mm [THT]"]
  S4 = Pushbutton [package="[THT]"]
  TRS1 = Audio Jack (TRS) 3.5mm [package="PG203J [THT]"]
  R4 = Rotary Potentiometer (Small) [maximum_resistance=100kΩ package=THT]
  R5 = Resistor [tolerance=±5% resistance=680 package=THT]
  R6 = Resistor [tolerance=±5% resistance=680 package=THT]
  R7 = Resistor [tolerance=±5% resistance=680 package=THT]
  R8 = Resistor [tolerance=±5% resistance=10k package=THT]
  R9 = Rotary Potentiometer (Small) [maximum_resistance=100kΩ package=THT]
  RHT1 = Humidity and Temperature Sensor RHT03

nets:
  N1: R1.Pin_0, R2.Pin_0, R3.Pin_0, LED1.cathode, LED2.cathode, LED3.cathode, TRS1.Sleeve, R4.leg2, R8.Pin_0, R9.leg2, RHT1.GND_1
  N2: R1.Pin_1, S1.Pin_3, S1.Pin_4, Part1.D8
  N3: R2.Pin_1, S3.Pin_3, S3.Pin_4, Part1.D6_PWM
  N4: R3.Pin_1, S2.Pin_3, S2.Pin_4, Part1.D7
  N5: S1.Pin_1, S1.Pin_2, S2.Pin_1, S2.Pin_2, S3.Pin_1, S3.Pin_2, S4.Pin_1, S4.Pin_2, R4.leg1, R9.leg1, RHT1.Vcc
  N6: Part1.A0, RHT1.Data-signal
  N7: Part1.A1, R9.wiper
  N8: Part1.A2, R4.wiper
  N9: Part1.A3, R5.Pin_0
  N10: Part1.A4/SDA, R6.Pin_0
  N11: Part1.A5/SCL, R7.Pin_0
  N12: Part1.D9_PWM, TRS1.Ring, TRS1.Tip
  N13: Part1.D5_PWM, LED1.anode, S4.Pin_3, S4.Pin_4, R7.Pin_1, R8.Pin_1
  N14: LED2.anode, R6.Pin_1
  N15: LED3.anode, R5.Pin_1

notes:
  Pretend this is the wind sensor...
