# Fritzing sketch TrombinoMouthpiece (saved by Fritzing 0.8.5b)
stripboards: 1
breadboards: 1

parts:
  Part1 = Arduino Uno (Rev3)
  LED1 = LED - 5mm [color="Red (633nm)" package="5 mm [THT]"]
  LED2 = LED - 5mm [color="Yellow (595nm)" package="5 mm [THT]"]
  LED3 = LED - 5mm [color="Green (570nm)" package="5 mm [THT]"]
  S4 = Pushbutton [package="[THT]"]
  TRS1 = Audio Jack (TRS) 3.5mm [package="PG203J [THT]"]
  R4 = Rotary Potentiometer (Small) [maximum_resistance=100kΩ package=THT]
  R5 = Resistor [tolerance=±5% resistance=680 package=THT]
  R6 = Resistor [tolerance=±5% resistance=680 package=THT]
  R7 = Resistor [tolerance=±5% resistance=680 package=THT]
  R8 = Resistor [tolerance=±5% resistance=10k package=THT]
  R9 = Rotary Potentiometer (Small) [maximum_resistance=100kΩ package=THT]
  J1 = Piezo Speaker
  R10 = Resistor [tolerance=±5% resistance=1M package=THT]

nets:
  N1: Part1.A0, J1.pin2, R10.Pin_1
  N2: Part1.A1, R9.wiper
  N3: Part1.A2, R4.wiper
  N4: Part1.A3, R5.Pin_0
  N5: Part1.A4/SDA, R6.Pin_0
  N6: Part1.A5/SCL, R7.Pin_0
  N7: Part1.D9_PWM, TRS1.Ring, TRS1.Tip
  N8: Part1.D5_PWM, LED1.anode, S4.Pin_3, S4.Pin_4, R7.Pin_1, R8.Pin_1
  N9: LED1.cathode, LED2.cathode, LED3.cathode, TRS1.Sleeve, R4.leg2, R8.Pin_0, R9.leg2, J1.pin1, R10.Pin_0
  N10: LED2.anode, R6.Pin_1
  N11: LED3.anode, R5.Pin_1
  N12: S4.Pin_1, S4.Pin_2, R4.leg1, R9.leg1
